# Fritzing sketch MAster (saved by Fritzing 0.9.3b)

parts:
  Part1 = Arduino Uno (Rev3) - ICSP
  Part2 = HC-05 [part_number=HC-05 package="breakout board"]
  S1 = Momentary Switch [package=ksa_sealed_tac_switch]
  R1 = Resistor [tolerance=±5% resistance=10k package="0603 [SMD]"]

nets:
  N1: Part1.D8, S1.4, R1.Pin_0
  N2: Part1.D0/RX, Part2.TXD
  N3: Part1.D1/TX, Part2.RXD
  5V: Part1.5V, Part2.VCC, S1.3
  GND: Part1.GND, Part2.GND, R1.Pin_1

custom parts:
  HC-05: A commonly available HC-05 Bluetooth breakout board.
