# Fritzing sketch Slave (saved by Fritzing 0.9.3b)

parts:
  Part2 = HC-05 [part_number=HC-05 package="breakout board"]
  LED1 = smd LED [color="Red (633nm)" package="0603 [SMD]"]
  R1 = Resistor [tolerance=±5% resistance=220 package="2512 [SMD]"]
  Part3 = Arduino Nano (Rev3.0) (ICSP)

nets:
  VCC: Part2.VCC, Part3.5V
  GND: Part2.GND, LED1.cathode, Part3.GND
  N1: Part2.TXD, Part3.D0/RX
  N2: Part2.RXD, Part3.D1/TX
  N3: LED1.anode, R1.Pin_1
  N4: R1.Pin_0, Part3.D13/SCK

custom parts:
  HC-05: A commonly available HC-05 Bluetooth breakout board.
